# Fritzing sketch project (saved by Fritzing 0.9.3b)
breadboards: 1

parts:
  Part1 = Arduino Nano (Rev3.0)
  LED1 = RGB LED (com. cathode, rgb) [package="5 mm [THT]"]
  LED2 = RGB LED (com. cathode, rgb) [package="5 mm [THT]"]
  LED3 = RGB LED (com. cathode, rgb) [package="5 mm [THT]"]
  LED4 = RGB LED (com. cathode, rgb) [package="5 mm [THT]"]
  LED5 = RGB LED (com. cathode, rgb) [package="5 mm [THT]"]
  LED6 = RGB LED (com. cathode, rgb) [package="5 mm [THT]"]
  LED7 = RGB LED (com. cathode, rgb) [package="5 mm [THT]"]
  LED8 = RGB LED (com. cathode, rgb) [package="5 mm [THT]"]
  LED9 = RGB LED (com. cathode, rgb) [package="5 mm [THT]"]
  LED10 = RGB LED (com. cathode, rgb) [package="5 mm [THT]"]
  LED11 = RGB LED (com. cathode, rgb) [package="5 mm [THT]"]
  LED12 = RGB LED (com. cathode, rgb) [package="5 mm [THT]"]
  R1 = Resistor [tolerance=±5% resistance=470 package=THT]
  R2 = Resistor [tolerance=±5% resistance=4.7k package=THT]
  R3 = Resistor [tolerance=±5% resistance=1.8k package=THT]
  S1 = Pushbutton [package=THT]
  R4 = Resistor [tolerance=±5% resistance=2.2k package=THT]
  Part2 = Real Time Clock Module - DS1307 RTC Breakout Board
  VCC1 = 4 x AAA Battery Mount

nets:
  GND: Part1.GND, S1.leg1, Part2.GND, VCC1.-
  N1: Part1.D2, Part2.SQW
  N2: Part1.D3, LED11.common_cathode
  N3: Part1.D4, LED10.common_cathode
  N4: Part1.D5, LED9.common_cathode
  N5: Part1.D6, LED7.common_cathode
  N6: Part1.D7, LED6.common_cathode
  N7: Part1.D8, R3.Pin_0
  N8: Part1.D9, LED8.common_cathode
  N9: Part1.D10, LED5.common_cathode
  N10: Part1.D11/MOSI, LED4.common_cathode
  N11: Part1.D12/MISO, LED1.common_cathode
  N12: Part1.VIN, VCC1.+
  5V: Part1.5V, Part1.A6, R4.Pin_1, Part2.5V
  N13: Part1.A7, S1.leg0, R4.Pin_0
  N14: Part1.A5, Part2.SCL
  N15: Part1.A4, Part2.SDA
  N16: Part1.A3, LED12.common_cathode
  N17: Part1.A2, R1.Pin_0
  N18: Part1.A1, LED2.common_cathode
  N19: Part1.A0, R2.Pin_0
  N20: Part1.D13/SCK, LED3.common_cathode
  N21: LED1.red_anode, LED2.red_anode, LED3.red_anode, LED4.red_anode, LED5.red_anode, LED6.red_anode, LED7.red_anode, LED8.red_anode, LED9.red_anode, LED10.red_anode, LED11.red_anode, LED12.red_anode, R1.Pin_1
  N22: LED1.green_anode, LED2.green_anode, LED3.green_anode, LED4.green_anode, LED5.green_anode, LED6.green_anode, LED7.green_anode, LED8.green_anode, LED9.green_anode, LED10.green_anode, LED11.green_anode, LED12.green_anode, R2.Pin_1
  N23: LED1.blue_anode, LED2.blue_anode, LED3.blue_anode, LED4.blue_anode, LED5.blue_anode, LED6.blue_anode, LED7.blue_anode, LED8.blue_anode, LED9.blue_anode, LED10.blue_anode, LED11.blue_anode, LED12.blue_anode, R3.Pin_1
